// Digital circuit ins5.dig as structural Verilog
module ins5 (
  input  In_1,
  input  In_2,
  output Y
);

  wire T1_d;

  PFET T1 (.G(In_1), .S(1'b1), .D(T1_d));
  PFET T2 (.G(In_2), .S(T1_d), .D(Y));
  NFET T4 (.G(In_2), .D(Y), .S(1'b0));
  NFET T3 (.G(In_1), .D(Y), .S(1'b0));
endmodule
