// Digital circuit ins7.dig as structural Verilog
// Gate Diffusion Input (GDI) xor
// {{de Gate Diffusion Input (GDI) xor}}
module ins7 (
  input  In_1,
  input  In_2,
  output Y
);

  wire pfet_1_d;

  PFET pfet_1 (.G(In_2), .S(1'b1), .D(pfet_1_d));
  NFET nfet_1 (.G(In_2), .D(pfet_1_d), .S(1'b0));
  PFET #(.unidirectional("true")) pfet_2 (.G(In_1), .S(In_2), .D(Y));
  NFET #(.unidirectional("true")) nfet_2 (.G(In_1), .D(Y), .S(pfet_1_d));
endmodule
